// Digital circuit ALU.dig as structural Verilog
module ALU (
  input  [3:0] A,
  input  [3:0] B,
  input  [1:0] S_1_S_0,
  input  Cin,
  output [3:0] D,
  output Cout
);

  wire [3:0] multiplexer_1_out, not_1_out, not_2_out;

  assign not_1_out = ~B;  // Not not_1, 4 bits wide
  assign not_2_out = ~4'b0000;  // Not not_2, 4 bits wide
  Multiplexer #(.Bits(4), .Selector_Bits(2)) multiplexer_1 (
    .sel(S_1_S_0), .in_0(B), .in_1(not_1_out), .in_2(4'b0000), .in_3(not_2_out), .out(multiplexer_1_out));
  // HW1_4_Bit_Ripple_Carry_Adder hw1_4_bit_ripple_carry_adder_1: pin names not known; wires that end beside it: A, multiplexer_1_out, Cin, D, Cout
endmodule
