// Digital circuit Register-File.dig as structural Verilog
module Register_File (
  input  [1:0] Read_Register_1,
  input  [1:0] Read_Register_2,
  input  [1:0] Write_Register,
  input  [7:0] Ctrl_Register,
  input  [3:0] Write_Data,
  input  Clock,
  output [3:0] Read_Data_1,
  output [3:0] Read_Data_2
);

  wire [3:0] demultiplexer_1_out_0, demultiplexer_1_out_1, demultiplexer_1_out_2, demultiplexer_1_out_3,
       R0_p4, R1_p4, R2_p4, R3_p4;

  Multiplexer #(.Bits(4), .Selector_Bits(2)) multiplexer_1 (
    .sel(Read_Register_1), .in_0(R0_p4), .in_1(R1_p4), .in_2(R2_p4), .in_3(R3_p4), .out(Read_Data_1));
  Demultiplexer #(.Bits(4), .Selector_Bits(2)) demultiplexer_1 (
    .sel(Write_Register), .in(Write_Data), .out_0(demultiplexer_1_out_0), .out_1(demultiplexer_1_out_1),
    .out_2(demultiplexer_1_out_2), .out_3(demultiplexer_1_out_3));
  // _4_Bit_GPR R0: pin names not known; wires that end beside it: Clock, demultiplexer_1_out_0, Ctrl_Register[1:0], R0_p4
  Multiplexer #(.Bits(4), .Selector_Bits(2)) multiplexer_2 (
    .sel(Read_Register_2), .in_0(R0_p4), .in_1(R1_p4), .in_2(R2_p4), .in_3(R3_p4), .out(Read_Data_2));
  // _4_Bit_GPR R1: pin names not known; wires that end beside it: Clock, demultiplexer_1_out_1, Ctrl_Register[3:2], R1_p4
  // _4_Bit_GPR R2: pin names not known; wires that end beside it: Clock, demultiplexer_1_out_2, Ctrl_Register[5:4], R2_p4
  // _4_Bit_GPR R3: pin names not known; wires that end beside it: Clock, demultiplexer_1_out_3, Ctrl_Register[7:6], R3_p4
endmodule
